# Fritzing sketch Rater (saved by Fritzing 0.9.1b)
breadboards: 1

parts:
  LED1 = RGB LED (com. cathode, rgb) [color="Infrared (940nm)" package="5 mm [THT]"]
  S2 = Pushbutton [package="[THT]"]
  S3 = Pushbutton [package="[THT]"]
  S1 = Pushbutton [package="[THT]"]
  R1 = Resistor [tolerance=±5% resistance=330 package=THT]
  R2 = Resistor [tolerance=±5% resistance=330 package=THT]
  R3 = Resistor [tolerance=±5% resistance=330 package=THT]
  R4 = Resistor [tolerance=±5% resistance=10k package=THT]
  R5 = Resistor [tolerance=±5% resistance=10k package=THT]
  R6 = Resistor [tolerance=±5% resistance=10k package=THT]
  T1 = TMP36 Temperature Sensor [package="TO92 [THT]"]
  Part2 = Arduino Board Ethernet

nets:
  N1: LED1.red_anode, R3.Pin_1
  GND: LED1.common_cathode, S2.Pin_1, S2.Pin_2, S3.Pin_1, S3.Pin_2, S1.Pin_1, S1.Pin_2, T1.GND, Part2.GND
  N2: LED1.green_anode, R1.Pin_1
  N3: LED1.blue_anode, R2.Pin_1
  N4: S2.Pin_3, S2.Pin_4, R5.Pin_1, Part2.D3_PWM
  N5: S3.Pin_3, S3.Pin_4, R6.Pin_1, Part2.D2_PWM
  N6: S1.Pin_3, S1.Pin_4, R4.Pin_1, Part2.D5_PWM
  N7: R1.Pin_0, Part2.D11/MOSI
  N8: R2.Pin_0, Part2.D10_PWM/SS
  N9: R3.Pin_0, Part2.D9_PWM
  N10: R4.Pin_0, R5.Pin_0, R6.Pin_0, T1.+Vs, Part2.5V
